# Fritzing sketch pcb (saved by Fritzing 0.9.3b)
circuit board: 5.22739cm x 5.21171cm
breadboards: 1

parts:
  J17 = female pin header, 4 pins [form="♀ (female)"]
  J18 = female pin header, 1 pin [form="♀ (female)"]
  J19 = female pin header, 1 pin [form="♀ (female)"]
  J20 = female pin header, 1 pin [form="♀ (female)"]
  J21 = female pin header, 1 pin [form="♀ (female)"]
  Componente2 = Arduino Uno (Rev3)
  IC1 = IC, DIP package, 8 pins [chip_label=IC]
  J22 = double row female pin header, 8 pins [form="♀ (female)"]
  J25 = female pin header, 1 pin [form="♀ (female)"]
  J26 = female pin header, 1 pin [form="♀ (female)"]
  J27 = female pin header, 1 pin [form="♀ (female)"]
  J28 = female pin header, 1 pin [form="♀ (female)"]
  J29 = female pin header, 2 pins [form="♀ (female)"]
  J24 = female pin header, 2 pins [form="♀ (female)"]
  J23 = female pin header, 2 pins [form="♀ (female)"]
  J30 = female pin header, 2 pins [form="♀ (female)"]
  J31 = female pin header, 2 pins [form="♀ (female)"]
  R1 = Resistor [tolerance=±5% resistance=220 package=THT]

nets:
  N1: J17.pin1, Componente2.5V, IC1.pin8, J24.pin1
  N2: J17.pin2, Componente2.A3
  N3: J17.pin3, J17.pin4, J19.pin1, J20.pin1, Componente2.GND, IC1.pin4, J22.pin4, J24.pin2, J31.pin2, R1.Pin_0
  N4: J18.pin1, IC1.pin5
  N5: J21.pin1, IC1.pin3
  N6: Componente2.A0, IC1.pin1, IC1.pin2
  N7: Componente2.A2, IC1.pin6, IC1.pin7
  N8: Componente2.A4/SDA, J29.pin2, J23.pin1
  N9: Componente2.A5/SCL, J29.pin1, J23.pin2
  N10: Componente2.D2, J28.pin1
  N11: Componente2.D3_PWM, J22.pin5
  N12: Componente2.D7, J30.pin1
  N13: Componente2.3V3, J26.pin1
  N14: Componente2.VIN, J31.pin1
  N15: J22.pin1, J27.pin1
  N16: J22.pin7, J22.pin8, J25.pin1
  N17: J30.pin2, R1.Pin_1
